// Logisim project cpu.circ as structural Verilog
module main (
  input  [3:0] A,
  input  [3:0] B,
  input  [3:0] O
);

  wire [3:0] alu_1_s;

  ALU alu_1 (.A(A), .B(B), .O(O), .S(alu_1_s));  // open: CF
  Hex_Digit_Display hex_digit_display_1 (.value(alu_1_s));  // open: dp
endmodule

module And (
  input  [3:0] A,
  input  [3:0] B,
  output [3:0] S
);

  and and_1 (S[0], A[0], B[0]);
  and and_2 (S[1], A[1], B[1]);
  and and_3 (S[2], A[2], B[2]);
  and and_4 (S[3], A[3], B[3]);
endmodule

module Or (
  input  [3:0] A,
  input  [3:0] B,
  output [3:0] S
);

  or or_1 (S[0], A[0], B[0]);
  or or_2 (S[1], A[1], B[1]);
  or or_3 (S[2], A[2], B[2]);
  or or_4 (S[3], A[3], B[3]);
endmodule

module Xor (
  input  [3:0] A,
  input  [3:0] B,
  output [3:0] S
);

  xor xor_1 (S[0], A[0], B[0]);
  xor xor_2 (S[1], A[1], B[1]);
  xor xor_3 (S[2], A[2], B[2]);
  xor xor_4 (S[3], A[3], B[3]);
endmodule

module Adder1 (
  input  A,
  input  B,
  output S,
  output C
);

  xor xor_1 (S, A, B);
  and and_1 (C, A, B);
endmodule

module Adder1C (
  input  A,
  input  B,
  input  C,
  output S,
  output C_2
);

  wire adder1_1_c, adder1_1_s, adder1_2_c;

  Adder1 adder1_1 (.A(A), .B(B), .S(adder1_1_s), .C(adder1_1_c));
  Adder1 adder1_2 (.A(adder1_1_s), .B(C), .S(S), .C(adder1_2_c));
  or or_1 (C_2, adder1_1_c, adder1_2_c);
endmodule

module Adder (
  input  [3:0] A,
  input  [3:0] B,
  output [3:0] S,
  output C
);

  wire adder1_1_c, adder1c_1_c_2, adder1c_2_c_2;

  Adder1 adder1_1 (.A(A[0]), .B(B[0]), .S(S[0]), .C(adder1_1_c));
  Adder1C adder1c_1 (.A(adder1_1_c), .B(A[1]), .C(B[1]), .S(S[1]), .C_2(adder1c_1_c_2));
  Adder1C adder1c_2 (.A(adder1c_1_c_2), .B(A[2]), .C(B[2]), .S(S[2]), .C_2(adder1c_2_c_2));
  Adder1C adder1c_3 (.A(adder1c_2_c_2), .B(A[3]), .C(B[3]), .S(S[3]), .C_2(C));
endmodule

module Transmission (
  input  O,
  input  [3:0] A,
  input  [3:0] B,
  output [3:0] Sa,
  output [3:0] Sb
);

  wire not_1_out;

  not not_1 (not_1_out, O);
  // Transmission_Gate #(.width(4)) transmission_1: pin names not known; wires that end beside it: A, O, not_1_out, O, Sa
  // Transmission_Gate #(.width(4)) transmission_2: pin names not known; wires that end beside it: B, not_1_out, O, Sb
endmodule

module ALU (
  input  [3:0] A,
  input  [3:0] B,
  input  [3:0] O,
  output [3:0] S,
  output CF
);

  wire [3:0] adder_1_s, and_1_s, or_1_s, xor_1_s;

  And and_1 (.A(A), .B(B), .S(and_1_s));
  Or or_1 (.A(A), .B(B), .S(or_1_s));
  Xor xor_1 (.A(A), .B(B), .S(xor_1_s));
  Adder adder_1 (.A(A), .B(B), .S(adder_1_s), .C(CF));
  Multiplexer #(.select(4), .width(4)) multiplexer_1 (
    .in0(and_1_s), .in1(or_1_s), .in2(xor_1_s), .in3(adder_1_s), .out(S), .sel(O), .en(1'b1));  // open: in4, in5, in6, in7, in8, in9, in10, in11, in12, in13, in14, in15
endmodule

module Bascule (
  input  D,
  input  C,
  output Q,
  output nQ
);

  wire not_1_out;

  not not_1 (not_1_out, C);
  // Transmission_Gate transmission_1: pin names not known; wires that end beside it: D, not_1_out, C, Q
  not not_2 (nQ, Q);
endmodule
